// Digital circuit Fulladder_sum.dig as structural Verilog
module Fulladder_sum (
  input  A,
  input  B,
  input  Cin
);

  wire _1, _2, _3, _4, _7400_1_pin3, _7400_1_pin9, _7400_1_pin10, _7400_1_pin13, _7400_3_pin3, _7400_3_pin9,
       _7400_3_pin10, not_1_out, not_2_out, not_3_out, not_6_out;

  not not_1 (not_1_out, A);
  not not_2 (not_2_out, B);
  not not_3 (not_3_out, Cin);
  _7400 _7400_1 (
    .pin1(not_1_out), .pin2(not_2_out), .pin3(_7400_1_pin3), .pin4(_7400_1_pin3), .pin5(not_3_out),
    .pin6(_1), .pin8(_2), .pin9(_7400_1_pin9), .pin10(_7400_1_pin10), .pin11(_7400_1_pin10), .pin12(B),
    .pin13(_7400_1_pin13));  // open: pin7, pin14
  // _7400 _7400_2: pin names not known; wires that end beside it: _3, _4, _2, _1
  not not_4 (_7400_1_pin13, A);
  not not_5 (_7400_1_pin9, Cin);
  not not_6 (not_6_out, B);
  _7400 _7400_3 (
    .pin1(A), .pin2(not_6_out), .pin3(_7400_3_pin3), .pin4(_7400_3_pin3), .pin5(Cin), .pin6(_3), .pin8(_4),
    .pin9(_7400_3_pin9), .pin10(_7400_3_pin10), .pin11(_7400_3_pin10), .pin12(B), .pin13(A));  // open: pin7, pin14
  not not_7 (_7400_3_pin9, Cin);
endmodule
