// Digital circuit Lab6.dig as structural Verilog
module Lab6 (
  input  [3:0] A,
  input  [3:0] B,
  input  C,
  input  [2:0] S,
  input  M,
  output [3:0] Z
);

  wire [3:0] A_1, A_1_t, A_B, A_B_1, A_plus_1, A_plus_B, A_plus_B_plus_1, A_t, AandB, AandNotB, AnandB,
       AnorB, AorB, AxnorB, B_plus_1, multiplexer_1_out, multiplexer_2_out, multiplexer_3_out,
       multiplexer_4_out, notA;

  Add #(.Bits(4)) add_1 (.a(A), .b(B), .c_i(1'b0), .s(A_plus_B));  // open: c_o
  Sub #(.Bits(4)) sub_1 (.a(A_t), .b(4'b0001), .c_i(1'b0), .s(A_1));  // open: c_o
  Sub #(.Bits(4)) sub_2 (.a(A), .b(4'b0001), .c_i(1'b0), .s(A_1_t));  // open: c_o
  Sub #(.Bits(4)) sub_3 (.a(A), .b(B), .c_i(1'b0), .s(A_B));  // open: c_o
  Sub #(.Bits(4)) sub_4 (.a(A_B), .b(4'b0001), .c_i(1'b0), .s(A_B_1));  // open: c_o
  Add #(.Bits(4)) add_2 (.a(4'b0000), .b(B), .c_i(1'b1), .s(B_plus_1));  // open: c_o
  Add #(.Bits(4)) add_3 (.a(4'b0000), .b(A), .c_i(1'b1), .s(A_plus_1));  // open: c_o
  Add #(.Bits(4)) add_4 (.a(A), .b(B), .c_i(1'b1), .s(A_plus_B_plus_1));  // open: c_o
  assign A_t = ~A;  // Not not_1, 4 bits wide
  assign notA = ~A;  // Not not_2, 4 bits wide
  assign AnandB = ~(A & B);  // NAnd nand_1, 4 bits wide
  assign AnorB = ~(A | B);  // NOr nor_1, 4 bits wide
  assign AxnorB = ~(A ^ B);  // XNOr xnor_1, 4 bits wide
  assign AandB = A & B;  // And and_1, 4 bits wide
  assign AorB = A | B;  // Or or_1, 4 bits wide
  assign AandNotB = A & ~B;  // And and_2, 4 bits wide
  Multiplexer #(.Bits(4), .Selector_Bits(3)) multiplexer_1 (
    .sel(S), .in_0(notA), .in_1(AnandB), .in_2(AnorB), .in_3(AxnorB), .in_4(AandB), .in_5(AorB),
    .in_6(AandNotB), .in_7(A), .out(multiplexer_1_out));
  Multiplexer #(.Selector_Bits(3), .Bits(4)) multiplexer_2 (
    .sel(S), .in_0(A), .in_1(A_1_t), .in_2(A_plus_B), .in_3(A_B_1), .in_4(A_1), .in_5(B),
    .in_6({A[2:0], 1'b0}), .in_7({1'b0, A[3:1]}), .out(multiplexer_2_out));
  Multiplexer #(.Selector_Bits(3), .Bits(4)) multiplexer_3 (
    .sel(S), .in_0(A_plus_1), .in_1(A), .in_2(A_plus_B_plus_1), .in_3(A_B), .in_4(A_t), .in_5(B_plus_1),
    .in_6({A[2:0], 1'b0}), .in_7({1'b0, A[3:1]}), .out(multiplexer_3_out));
  Multiplexer #(.Bits(4)) multiplexer_4 (
    .sel(C), .in_0(multiplexer_1_out), .in_1(multiplexer_2_out), .out(multiplexer_4_out));
  Multiplexer #(.Bits(4)) multiplexer_5 (.sel(M), .in_0(multiplexer_4_out), .in_1(multiplexer_3_out), .out(Z));

  // Other names for the same wires on the sheet: ShiftAleft[3:1] = A[2:0]; ShiftAright[2:0] = A[3:1]
endmodule
