// Digital circuit diglab_02_03.dig as structural Verilog
module diglab_02_03 (
  input  B,
  input  Cin,
  input  A,
  output Sum,
  output Cout
);

  wire and_1_out, and_2_out, and_3_out, and_4_out, and_5_out, and_6_out, and_7_out, and_8_out, not_1_out,
       not_2_out, not_3_out, not_4_out, not_5_out, not_6_out, not_7_out, not_8_out, not_9_out;

  not not_1 (not_1_out, A);
  not not_2 (not_2_out, B);
  not not_3 (not_3_out, Cin);
  not not_4 (not_4_out, A);
  not not_5 (not_5_out, B);
  not not_6 (not_6_out, A);
  not not_7 (not_7_out, Cin);
  not not_8 (not_8_out, B);
  not not_9 (not_9_out, Cin);
  and and_1 (and_1_out, not_1_out, B, Cin);
  and and_2 (and_2_out, A, not_2_out, Cin);
  and and_3 (and_3_out, A, B, not_3_out);
  and and_4 (and_4_out, A, B, Cin);
  and and_5 (and_5_out, not_4_out, not_5_out, Cin);
  and and_6 (and_6_out, not_6_out, B, not_7_out);
  and and_7 (and_7_out, A, not_8_out, not_9_out);
  and and_8 (and_8_out, A, B, Cin);
  or or_1 (Cout, and_1_out, and_2_out, and_3_out, and_4_out);
  or or_2 (Sum, and_5_out, and_6_out, and_7_out, and_8_out);
endmodule
