// Digital circuit diglab_03_01.dig as structural Verilog
module diglab_03_01 (
  input  [3:0] In,
  output A,
  output B,
  output C,
  output D,
  output E,
  output F,
  output G
);

  wire and_1_out, and_2_out, and_3_out, and_4_out, not_1_out, not_2_out, not_3_out, not_4_out, not_5_out,
       not_6_out, not_7_out, not_8_out, not_9_out, not_10_out, not_11_out, not_12_out, not_13_out,
       not_14_out, not_15_out, not_16_out, not_17_out, not_18_out, not_19_out, not_20_out, not_21_out,
       not_22_out, not_23_out, not_24_out, not_25_out, not_26_out, not_27_out, not_28_out, not_29_out,
       not_30_out, not_31_out, not_32_out, or_1_out, or_2_out, or_3_out, or_4_out, or_6_out, or_7_out,
       or_8_out, or_9_out, or_10_out, or_11_out, or_12_out, or_13_out, or_14_out;

  not not_1 (not_1_out, In[0]);
  not not_2 (not_2_out, In[2]);
  not not_3 (not_3_out, In[0]);
  not not_4 (not_4_out, In[2]);
  not not_5 (not_5_out, In[1]);
  not not_6 (not_6_out, In[2]);
  not not_7 (not_7_out, In[1]);
  not not_8 (not_8_out, In[0]);
  not not_9 (not_9_out, In[2]);
  not not_10 (not_10_out, In[0]);
  not not_11 (not_11_out, In[1]);
  not not_12 (not_12_out, In[2]);
  not not_13 (not_13_out, In[0]);
  not not_14 (not_14_out, In[1]);
  not not_15 (not_15_out, In[2]);
  not not_16 (not_16_out, In[3]);
  not not_17 (not_17_out, In[0]);
  not not_18 (not_18_out, In[2]);
  not not_19 (not_19_out, In[3]);
  not not_20 (not_20_out, In[0]);
  not not_21 (not_21_out, In[3]);
  not not_22 (not_22_out, In[0]);
  not not_23 (not_23_out, In[1]);
  not not_24 (not_24_out, In[2]);
  not not_25 (not_25_out, In[0]);
  not not_26 (not_26_out, In[1]);
  not not_27 (not_27_out, In[0]);
  not not_28 (not_28_out, In[1]);
  or or_1 (or_1_out, not_1_out, In[1], In[2], In[3]);
  or or_2 (or_2_out, In[0], In[1], not_2_out, In[3]);
  or or_3 (or_3_out, not_3_out, In[1], not_4_out, In[3]);
  or or_4 (or_4_out, In[0], not_5_out, not_6_out, In[3]);
  or or_5 (C, In[0], not_7_out, In[2], In[3]);
  or or_6 (or_6_out, not_8_out, In[1], In[2], In[3]);
  or or_7 (or_7_out, In[0], In[1], not_9_out, In[3]);
  or or_8 (or_8_out, not_10_out, not_11_out, not_12_out, In[3]);
  and and_1 (and_1_out, not_13_out, not_14_out, not_15_out, not_16_out);
  and and_2 (and_2_out, not_17_out, In[1], not_18_out, not_19_out);
  and and_3 (and_3_out, not_20_out, In[1], In[2], not_21_out);
  and and_4 (and_4_out, not_22_out, not_23_out, not_24_out, In[3]);
  or or_9 (or_9_out, not_25_out, In[1], In[2], In[3]);
  or or_10 (or_10_out, In[0], not_26_out, In[2], In[3]);
  or or_11 (or_11_out, not_27_out, not_28_out, In[2], In[3]);
  or or_12 (or_12_out, In[0], In[1], In[2], In[3]);
  or or_13 (or_13_out, not_29_out, In[1], In[2], In[3]);
  not not_29 (not_29_out, In[0]);
  or or_14 (or_14_out, not_30_out, not_31_out, not_32_out, In[3]);
  not not_30 (not_30_out, In[0]);
  not not_31 (not_31_out, In[1]);
  not not_32 (not_32_out, In[2]);
  and and_5 (A, or_1_out, or_2_out);
  and and_6 (B, or_3_out, or_4_out);
  and and_7 (D, or_6_out, or_7_out, or_8_out);
  or or_15 (E, and_1_out, and_2_out, and_3_out, and_4_out);
  and and_8 (F, or_9_out, or_10_out, or_11_out);
  and and_9 (G, or_12_out, or_13_out, or_14_out);
endmodule
