// Digital circuit diglab_03_03.dig as structural Verilog
module diglab_03_03 (
  input  [1:0] Selector,
  input  [3:0] In,
  output [3:0] Output
);

  wire and_1_out, and_2_out, and_3_out, and_4_out, and_5_out, and_6_out, and_7_out, and_8_out, and_9_out,
       and_10_out, and_11_out, and_12_out, and_13_out, and_14_out, and_15_out, and_16_out, and_17_out,
       and_18_out, and_19_out, and_20_out, and_21_out, and_22_out, and_23_out, and_24_out, and_25_out,
       and_26_out, and_27_out, and_28_out, and_29_out, and_30_out, and_32_out, and_33_out, and_34_out,
       and_35_out, and_36_out, and_37_out, and_38_out, and_39_out, and_40_out, and_41_out, and_42_out,
       not_1_out, not_2_out, not_3_out, not_4_out, not_5_out, not_6_out, not_7_out, not_8_out, not_9_out,
       not_10_out, not_11_out, not_12_out, not_13_out, not_14_out, not_15_out, not_16_out, not_17_out,
       not_18_out, not_19_out, not_20_out, not_21_out, not_22_out, not_23_out, not_24_out, not_25_out,
       not_26_out, not_27_out, not_28_out, not_29_out, not_30_out, not_31_out, not_32_out, not_33_out,
       not_34_out, not_35_out, not_36_out, not_37_out, not_38_out, not_39_out, not_40_out, not_41_out,
       not_42_out, not_43_out, not_44_out, not_45_out, not_46_out, not_47_out, not_48_out, not_49_out,
       not_50_out, not_51_out, not_52_out, not_53_out, not_54_out, not_55_out, not_56_out, not_57_out,
       not_58_out, not_59_out, not_60_out, not_61_out, not_62_out, not_63_out, not_64_out, not_65_out,
       not_66_out, not_67_out, not_68_out, not_69_out, not_70_out, not_71_out, not_72_out, not_73_out,
       not_74_out, not_75_out, not_76_out, not_77_out, not_78_out, not_79_out, not_80_out, not_81_out,
       not_82_out;
  wire [3:0] _642_3code, _2421code, and_47_out, and_48_out, and_49_out, and_50_out, Cyclic, Excess_3;
  wire [3:3] and_43_out, and_44_out, and_45_out, and_46_out;

  not not_1 (not_1_out, In[2]);
  not not_2 (not_2_out, In[1]);
  not not_3 (not_3_out, In[3]);
  not not_4 (not_4_out, In[3]);
  not not_5 (not_5_out, In[2]);
  not not_6 (not_6_out, In[3]);
  not not_7 (not_7_out, In[1]);
  not not_8 (not_8_out, In[2]);
  not not_9 (not_9_out, In[1]);
  not not_10 (not_10_out, In[3]);
  not not_11 (not_11_out, In[0]);
  not not_12 (not_12_out, In[3]);
  not not_13 (not_13_out, In[2]);
  not not_14 (not_14_out, In[1]);
  not not_15 (not_15_out, In[3]);
  not not_16 (not_16_out, In[1]);
  not not_17 (not_17_out, In[3]);
  not not_18 (not_18_out, In[2]);
  not not_19 (not_19_out, In[1]);
  and and_1 (and_1_out, not_1_out, not_2_out, In[0]);
  and and_2 (and_2_out, not_3_out, In[0]);
  and and_3 (and_3_out, not_4_out, not_5_out, In[1]);
  and and_4 (and_4_out, not_6_out, In[2], not_7_out, In[0]);
  and and_5 (and_5_out, In[3], not_8_out, not_9_out);
  and and_6 (and_6_out, not_10_out, In[2], not_11_out);
  and and_7 (and_7_out, not_12_out, In[2], In[1]);
  and and_8 (and_8_out, In[3], not_13_out, not_14_out);
  and and_9 (and_9_out, not_15_out, In[2], not_16_out, In[0]);
  and and_10 (and_10_out, not_17_out, In[2], In[1]);
  and and_11 (and_11_out, In[3], not_18_out, not_19_out);
  or or_1 (_2421code[0], and_1_out, and_2_out);
  or or_2 (_2421code[1], and_3_out, and_4_out, and_5_out);
  or or_3 (_2421code[2], and_6_out, and_7_out, and_8_out);
  or or_4 (_2421code[3], and_9_out, and_10_out, and_11_out);
  not not_20 (not_20_out, In[2]);
  not not_21 (not_21_out, In[1]);
  not not_22 (not_22_out, In[3]);
  not not_23 (not_23_out, In[1]);
  not not_24 (not_24_out, In[3]);
  not not_25 (not_25_out, In[2]);
  not not_26 (not_26_out, In[1]);
  not not_27 (not_27_out, In[3]);
  not not_28 (not_28_out, In[0]);
  not not_29 (not_29_out, In[3]);
  not not_30 (not_30_out, In[1]);
  not not_31 (not_31_out, In[3]);
  not not_32 (not_32_out, In[3]);
  not not_33 (not_33_out, In[0]);
  not not_34 (not_34_out, In[2]);
  not not_35 (not_35_out, In[1]);
  not not_36 (not_36_out, In[2]);
  not not_37 (not_37_out, In[1]);
  not not_38 (not_38_out, In[3]);
  not not_39 (not_39_out, In[1]);
  not not_40 (not_40_out, In[3]);
  and and_12 (and_12_out, not_20_out, not_21_out, In[0]);
  and and_13 (and_13_out, not_22_out, In[2], not_23_out, In[0]);
  and and_14 (and_14_out, not_24_out, In[1], In[0]);
  and and_15 (and_15_out, In[3], not_25_out, not_26_out);
  and and_16 (and_16_out, not_27_out, In[1], not_28_out);
  and and_17 (and_17_out, not_29_out, In[2], not_30_out, In[0]);
  and and_18 (and_18_out, not_31_out, In[2], In[1]);
  and and_19 (and_19_out, not_32_out, In[2], not_33_out);
  and and_20 (and_20_out, not_34_out, not_35_out, In[0]);
  and and_21 (and_21_out, In[3], not_36_out, not_37_out);
  and and_22 (and_22_out, not_38_out, In[2], not_39_out, In[0]);
  and and_23 (and_23_out, not_40_out, In[1], In[0]);
  or or_5 (_642_3code[0], and_12_out, and_13_out, and_14_out);
  or or_6 (_642_3code[1], and_15_out, and_16_out, and_17_out);
  or or_7 (_642_3code[2], and_18_out, and_19_out, and_20_out);
  or or_8 (_642_3code[3], and_21_out, and_22_out, and_23_out);
  not not_41 (not_41_out, In[3]);
  not not_42 (not_42_out, In[1]);
  not not_43 (not_43_out, In[3]);
  not not_44 (not_44_out, In[0]);
  not not_45 (not_45_out, In[2]);
  not not_46 (not_46_out, In[1]);
  not not_47 (not_47_out, In[3]);
  not not_48 (not_48_out, In[2]);
  not not_49 (not_49_out, In[3]);
  not not_50 (not_50_out, In[1]);
  not not_51 (not_51_out, In[2]);
  not not_52 (not_52_out, In[1]);
  not not_53 (not_53_out, In[3]);
  not not_54 (not_54_out, In[2]);
  not not_55 (not_55_out, In[1]);
  and and_24 (and_24_out, not_41_out, not_42_out, In[0]);
  and and_25 (and_25_out, not_43_out, In[1], not_44_out);
  and and_26 (and_26_out, not_45_out, not_46_out, In[0]);
  and and_27 (and_27_out, not_47_out, not_48_out, In[1]);
  and and_28 (and_28_out, not_49_out, In[2], not_50_out);
  and and_29 (and_29_out, In[3], not_51_out, not_52_out);
  and and_30 (and_30_out, not_53_out, In[2]);
  and and_31 (Cyclic[3], In[3], not_54_out, not_55_out);
  or or_9 (Cyclic[0], and_24_out, and_25_out, and_26_out);
  or or_10 (Cyclic[1], and_27_out, and_28_out);
  or or_11 (Cyclic[2], and_29_out, and_30_out);
  and and_32 (and_32_out, not_56_out, not_57_out, not_58_out);
  not not_56 (not_56_out, In[2]);
  not not_57 (not_57_out, In[1]);
  not not_58 (not_58_out, In[0]);
  and and_33 (and_33_out, not_59_out, not_60_out);
  not not_59 (not_59_out, In[3]);
  not not_60 (not_60_out, In[0]);
  and and_34 (and_34_out, not_61_out, In[2], not_62_out, not_63_out);
  not not_61 (not_61_out, In[3]);
  not not_62 (not_62_out, In[1]);
  not not_63 (not_63_out, In[0]);
  and and_35 (and_35_out, not_64_out, In[1], In[0]);
  not not_64 (not_64_out, In[3]);
  and and_36 (and_36_out, not_65_out, not_66_out, not_67_out);
  not not_65 (not_65_out, In[2]);
  not not_66 (not_66_out, In[1]);
  not not_67 (not_67_out, In[0]);
  and and_37 (and_37_out, not_68_out, not_69_out, In[0]);
  not not_68 (not_68_out, In[2]);
  not not_69 (not_69_out, In[1]);
  and and_38 (and_38_out, not_70_out, In[2], not_71_out, not_72_out);
  not not_70 (not_70_out, In[3]);
  not not_71 (not_71_out, In[1]);
  not not_72 (not_72_out, In[0]);
  and and_39 (and_39_out, not_73_out, not_74_out, In[1]);
  not not_73 (not_73_out, In[3]);
  not not_74 (not_74_out, In[2]);
  and and_40 (and_40_out, not_75_out, In[2], In[1]);
  not not_75 (not_75_out, In[3]);
  and and_41 (and_41_out, In[3], not_76_out, not_77_out);
  not not_76 (not_76_out, In[2]);
  not not_77 (not_77_out, In[1]);
  and and_42 (and_42_out, not_78_out, In[2], In[0]);
  not not_78 (not_78_out, In[3]);
  or or_12 (Excess_3[0], and_32_out, and_33_out);
  or or_13 (Excess_3[1], and_34_out, and_35_out, and_36_out);
  or or_14 (Excess_3[2], and_37_out, and_38_out, and_39_out);
  or or_15 (Excess_3[3], and_40_out, and_41_out, and_42_out);
  not not_79 (not_79_out, Selector[0]);
  not not_80 (not_80_out, Selector[1]);
  not not_81 (not_81_out, Selector[1]);
  not not_82 (not_82_out, Selector[0]);
  and and_43 (and_43_out[3], not_79_out, not_80_out);
  and and_44 (and_44_out[3], Selector[0], not_81_out);
  and and_45 (and_45_out[3], not_82_out, Selector[1]);
  and and_46 (and_46_out[3], Selector[0], Selector[1]);
  assign and_47_out = Excess_3 & {4{and_43_out[3]}};  // And and_47, 4 bits wide
  assign and_48_out = Cyclic & {4{and_44_out[3]}};  // And and_48, 4 bits wide
  assign and_49_out = _2421code & {4{and_45_out[3]}};  // And and_49, 4 bits wide
  assign and_50_out = _642_3code & {4{and_46_out[3]}};  // And and_50, 4 bits wide
  assign Output = and_47_out | and_48_out | and_49_out | and_50_out;  // Or or_16, 4 bits wide
endmodule
