// Digital circuit diglab_03_04.dig as structural Verilog
module diglab_03_04 (
  input  [6:0] In,
  output [6:0] Output
);

  wire not_1_out, not_2_out, not_3_out, not_4_out, not_5_out, not_6_out, not_7_out, not_8_out, not_9_out,
       xor_1_out, xor_2_out, xor_3_out;
  wire [6:0] and_2_out;

  xor xor_1 (xor_1_out, In[3], In[2], In[1], In[0]);
  xor xor_2 (xor_2_out, In[5], In[4], In[1], In[0]);
  xor xor_3 (xor_3_out, In[6], In[4], In[2], In[0]);
  and and_1 (and_2_out[0], xor_1_out, xor_2_out, xor_3_out);
  and and_2 (and_2_out[1], xor_1_out, xor_2_out, not_1_out);
  not not_1 (not_1_out, xor_3_out);
  and and_3 (and_2_out[2], xor_1_out, not_2_out, xor_3_out);
  not not_2 (not_2_out, xor_2_out);
  and and_4 (and_2_out[3], xor_1_out, not_3_out, not_4_out);
  not not_3 (not_3_out, xor_2_out);
  not not_4 (not_4_out, xor_3_out);
  and and_5 (and_2_out[4], not_5_out, xor_2_out, xor_3_out);
  not not_5 (not_5_out, xor_1_out);
  and and_6 (and_2_out[5], not_6_out, xor_2_out, not_7_out);
  not not_6 (not_6_out, xor_1_out);
  not not_7 (not_7_out, xor_3_out);
  and and_7 (and_2_out[6], not_8_out, not_9_out, xor_3_out);
  not not_8 (not_8_out, xor_1_out);
  not not_9 (not_9_out, xor_2_out);
  assign Output = In ^ and_2_out;  // XOr xor_4, 7 bits wide
endmodule
