// Digital circuit diglab_05_01.dig as structural Verilog
module diglab_05_01 (
  input  A,
  input  B,
  input  C,
  input  D,
  output Before,
  output After
);

  wire and_1_out, and_2_out, and_3_out, and_4_out;

  and and_1 (and_1_out, ~C, D);  // And
  and and_2 (and_2_out, A, ~B, D);  // And
  and and_3 (and_3_out, ~C, D);  // And
  and and_4 (and_4_out, D, ~B);  // And
  or or_1 (Before, and_1_out, ~A, and_2_out);  // Or
  or or_2 (After, and_3_out, ~A, and_4_out);  // Or
endmodule

/* Test case T2:
A B C D After
0 0 0 0 1 
0 0 0 1 1 
0 0 1 0 1 
0 0 1 1 1 
0 1 0 0 1 
0 1 0 1 1 
0 1 1 0 1 
0 1 1 1 1 

1 0 0 1 1 

1 0 1 1 1 

1 1 0 1 1
*/

/* Test case T1:
A B C D Before
0 0 1 1 1
1 0 1 1 1
1 0 1 1 1
*/
