// Digital circuit diglab_06_01.dig as structural Verilog
module diglab_06_01 (
  input  [3:0] A,
  input  [3:0] B,
  input  [2:0] S,
  input  M,
  input  C,
  output [3:0] F,
  output Cout
);

  wire [3:0] _3, _4, _5, _6, A_1, A_1_t, A_B, A_B_1, A_plus_1, A_plus_B, A_plus_B_plus_1, A_t, B_plus_1, m1,
       multiplexer_1_out, multiplexer_3_out, multiplexer_4_out, no1, no2, notA, shiftleft, shiftright;

  assign no1 = ~(A & B);  // NAnd nand_1, 4 bits wide
  assign no2 = ~(A | B);  // NOr nor_1, 4 bits wide
  assign _3 = ~(A ^ B);  // XNOr xnor_1, 4 bits wide
  assign _4 = A & B;  // And and_1, 4 bits wide
  assign _5 = A | B;  // Or or_1, 4 bits wide
  assign _6 = A & ~B;  // And and_2, 4 bits wide
  Multiplexer #(.Selector_Bits(3), .Bits(4)) multiplexer_1 (
    .sel(S), .in_0(notA), .in_1(no1), .in_2(no2), .in_3(_3), .in_4(_4), .in_5(_5), .in_6(_6), .in_7(A),
    .out(multiplexer_1_out));
  not not_1 (notA[0], A[0]);
  not not_2 (notA[1], A[1]);
  not not_3 (notA[2], A[2]);
  not not_4 (notA[3], A[3]);
  Multiplexer #(.Bits(4)) multiplexer_2 (.sel(M), .in_0(multiplexer_1_out), .in_1(m1), .out(F));
  Add #(.Bits(4)) add_1 (.a(A), .b(4'b0001), .c_i(1'b0), .s(A_plus_1));  // open: c_o
  Sub #(.Bits(4)) sub_1 (.a(A), .b(B), .c_i(1'b0), .s(A_B));  // open: c_o
  Add #(.Bits(4)) add_2 (.a(B), .b(4'b0001), .c_i(1'b0), .s(B_plus_1));  // open: c_o
  Multiplexer #(.Selector_Bits(3), .Bits(4)) multiplexer_3 (
    .sel(S), .in_0(A), .in_1(A_1_t), .in_2(A_plus_B), .in_3(A_B_1), .in_4(A_1), .in_5(B), .in_6(shiftleft),
    .in_7(shiftright), .out(multiplexer_3_out));
  Multiplexer #(.Selector_Bits(3), .Bits(4)) multiplexer_4 (
    .sel(S), .in_0(A_plus_1), .in_1(A), .in_2(A_plus_B_plus_1), .in_3(A_B), .in_4(A_t), .in_5(B_plus_1),
    .in_6(shiftleft), .in_7(shiftright), .out(multiplexer_4_out));
  Sub #(.Bits(4)) sub_2 (.a(A), .b(4'b0001), .c_i(1'b0), .s(A_1_t));  // open: c_o
  Add #(.Bits(4)) add_3 (.a(A), .b(B), .c_i(1'b0), .s(A_plus_B));  // open: c_o
  Sub #(.Bits(4)) sub_3 (.a(A), .b(B), .c_i(1'b0), .s(A_B));  // open: c_o
  LookUpTable #(.Bits(4)) Shift_A_left_1_bit (.in0(A[0]), .in1(A[1]), .in2(A[2]), .in3(A[3]), .out(shiftleft));
  LookUpTable #(.Bits(4)) Shift_A_right1_bit (.in0(A[0]), .in1(A[1]), .in2(A[2]), .in3(A[3]), .out(shiftright));
  Add #(.Bits(4)) add_4 (.a(A_plus_1), .b(B), .c_i(1'b0), .s(A_plus_B_plus_1));  // open: c_o
  LookUpTable #(.Bits(4)) lookuptable_1 (.in0(A[0]), .in1(A[1]), .in2(A[2]), .in3(A[3]), .out(A_t));
  Sub #(.Bits(4)) sub_4 (.a(A_B), .b(4'b0001), .c_i(1'b0), .s(A_B_1));  // open: c_o
  Multiplexer #(.Bits(4)) multiplexer_5 (.sel(C), .in_0(multiplexer_3_out), .in_1(multiplexer_4_out), .out(m1));
  Sub #(.Bits(4)) sub_5 (.a(A_t), .b(4'b0001), .c_i(1'b0), .s(A_1));  // open: c_o

  assign Cout = 1'b0;

  // Notes on the sheet:
  //   contents of Shift_A_left_1_bit (hex, n*v repeats v):
  //   0,2,4,6,8,fffffffffffffffa,fffffffffffffffc,e,0,2,4,6,8,a,c,e
  //   contents of Shift_A_right1_bit (hex, n*v repeats v):
  //   0,0,1,1,2,2,3,3,4,4,5,5,6,6,7,7
  //   contents of lookuptable_1 (hex, n*v repeats v):
  //   0,ffffffffffffffff,fffffffffffffffe,fffffffffffffffd,fffffffffffffffc
  //   ,fffffffffffffffb,fffffffffffffffa,9,8,7,6,5,4,3,2,1
endmodule
