// Digital circuit diglab_08_01.dig as structural Verilog
module diglab_08_01 (
  input  P,
  input  T,
  input  A,
  input  B,
  input  C,
  input  D,
  input  Clr,
  input  Load,
  input  Clock,
  output QA,
  output QB,
  output QC,
  output QD,
  output RCO
);

  wire not_1_out, not_2_out, or_1_out;
  wire [0:0] and_1_out;
  wire [3:0] add_1_s, and_2_out, multiplexer_1_out;
  wire [3:3] or_2_out;

  and and_1 (and_1_out[0], P, T, Clr, Load);
  not not_1 (not_1_out, Clr);
  not not_2 (not_2_out, Load);
  or or_1 (or_1_out, not_1_out, not_2_out);
  or or_2 (or_2_out[3], Clr, ~Load);  // Or
  Add #(.Bits(4)) add_1 (.a(multiplexer_1_out), .b({3'b000, and_1_out[0]}), .c_i(1'b0), .s(add_1_s));  // open: c_o
  assign and_2_out = {4{or_2_out[3]}} & {D, C, B, A};  // And and_2, 4 bits wide
  Multiplexer #(.Bits(4)) multiplexer_1 (
    .sel(or_1_out), .in_0({QD, QC, QB, QA}), .in_1(and_2_out), .out(multiplexer_1_out));
  D_FF #(.Bits(4)) d_ff_1 (.D(add_1_s), .C(Clock), .Q({QD, QC, QB, QA}));  // open: nQ
  and and_3 (RCO, QA, QB, QC, QD);
endmodule
