// Digital circuit diglab_08_02.dig as structural Verilog
module diglab_08_02 (
  input  A,
  input  B,
  input  Clock,
  input  Clr,
  output Z
);

  wire add_1_c_o, and_1_out, and_2_out, and_3_out, d_ff_1_q;

  and and_1 (and_1_out, Clr, A);
  and and_2 (and_2_out, Clr, B);
  Add add_1 (.a(and_1_out), .b(and_2_out), .c_i(d_ff_1_q), .s(Z), .c_o(add_1_c_o));
  D_FF d_ff_1 (.D(and_3_out), .C(Clock), .Q(d_ff_1_q));  // open: nQ
  and and_3 (and_3_out, Clr, add_1_c_o);

  // Other names for the same wires on the sheet: clk = Clock
endmodule
