// Digital circuit diglab_08_04.dig as structural Verilog
module diglab_08_04 (
  input  clock,
  input  Clr,
  input  P,
  output Z
);

  wire and_1_out, and_2_out, d_ff_1_q, d_ff_2_nq, d_ff_3_q;

  D_FF d_ff_1 (.D(P), .C(clock), .Q(d_ff_1_q));  // open: nQ
  and and_1 (and_1_out, ~Clr, d_ff_1_q);  // And
  and and_2 (and_2_out, d_ff_3_q, ~Clr);  // And
  D_FF d_ff_2 (.D(and_2_out), .C(clock), .nQ(d_ff_2_nq));  // open: Q
  D_FF d_ff_3 (.D(and_1_out), .C(clock), .Q(d_ff_3_q));  // open: nQ
  and and_3 (Z, d_ff_2_nq, d_ff_3_q);
endmodule
