// Digital circuit exam2563Q1.dig as structural Verilog
module exam2563Q1 (
  input  [15:0] A,
  input  \input ,
  input  reset,
  input  clk,
  output [15:0] second,
  output [15:0] first
);

  wire and_1_out, and_2_out, and_3_out, comparator_1_gt, comparator_1_lt, comparator_2_gt, comparator_3_gt,
       or_1_out, or_2_out, or_3_out;
  wire [15:0] A_plus, multiplexer_2_out, multiplexer_3_out, multiplexer_4_out, register_2_q, register_3_q;

  Multiplexer #(.Bits(16)) multiplexer_1 (.sel(reset), .in_0(A), .in_1({16{1'b0}}), .out(A_plus));
  Multiplexer #(.Bits(16)) multiplexer_2 (.sel(reset), .in_0(first), .in_1({16{1'b0}}), .out(multiplexer_2_out));
  Multiplexer #(.Bits(16)) multiplexer_3 (.sel(reset), .in_0(A), .in_1({16{1'b0}}), .out(multiplexer_3_out));
  Comparator #(.Bits(16)) comparator_1 (
    .a(A_plus), .b(multiplexer_2_out), .gt(comparator_1_gt), .lt(comparator_1_lt));  // open: eq
  Multiplexer #(.Bits(16)) multiplexer_4 (.sel(reset), .in_0(second), .in_1({16{1'b0}}), .out(multiplexer_4_out));
  Comparator #(.Bits(16)) comparator_2 (
    .a(multiplexer_3_out), .b(multiplexer_4_out), .gt(comparator_2_gt));  // open: eq, lt
  and and_1 (and_1_out, comparator_1_gt, \input );
  and and_2 (and_2_out, comparator_1_gt, \input );
  and and_3 (and_3_out, comparator_1_lt, \input , comparator_2_gt);
  or or_1 (or_1_out, and_1_out, reset);
  Register #(.Bits(16)) register_1 (.D(A_plus), .C(clk), .en(or_1_out), .Q(first));
  or or_2 (or_2_out, and_2_out, reset);
  or or_3 (or_3_out, and_3_out, reset);
  Register #(.Bits(16)) register_2 (.D(first), .C(clk), .en(or_2_out), .Q(register_2_q));
  Register #(.Bits(16)) register_3 (.D(A_plus), .C(clk), .en(or_3_out), .Q(register_3_q));
  Comparator #(.Bits(16)) comparator_3 (.a(register_2_q), .b(register_3_q), .gt(comparator_3_gt));  // open: eq, lt
  Multiplexer #(.Bits(16)) multiplexer_5 (
    .sel(comparator_3_gt), .in_0(register_3_q), .in_1(register_2_q), .out(second));

  // Other names for the same wires on the sheet: max1[15:0] = first; max2[15:0] = second
endmodule
