// Digital circuit finalcedtq1.dig as structural Verilog
module finalcedtq1 (
  input  clock,
  input  X,
  input  Y,
  input  Z,
  input  load,
  input  reset,
  output A,
  output B,
  output C
);

  wire and_1_out, and_2_out, and_3_out, and_4_out, and_5_out, multiplexer_1_out, multiplexer_2_out,
       multiplexer_3_out, multiplexer_4_out, multiplexer_5_out, multiplexer_6_out, not_1_out, not_2_out,
       not_3_out, or_1_out, or_2_out, or_3_out;

  not not_1 (not_1_out, A);
  not not_2 (not_2_out, B);
  not not_3 (not_3_out, C);
  and and_1 (and_1_out, C, not_1_out);
  and and_2 (and_2_out, C, not_2_out);
  and and_3 (and_3_out, not_3_out, B, A);
  and and_4 (and_4_out, not_2_out, A);
  and and_5 (and_5_out, C, A);
  or or_1 (or_1_out, and_1_out, and_2_out, and_3_out);
  or or_2 (or_2_out, not_3_out, and_4_out);
  or or_3 (or_3_out, and_5_out, B);
  Multiplexer multiplexer_1 (.sel(load), .in_0(or_1_out), .in_1(X), .out(multiplexer_1_out));
  Multiplexer multiplexer_2 (.sel(load), .in_0(or_2_out), .in_1(Y), .out(multiplexer_2_out));
  Multiplexer multiplexer_3 (.sel(load), .in_0(or_3_out), .in_1(Z), .out(multiplexer_3_out));
  Multiplexer multiplexer_4 (.sel(reset), .in_0(multiplexer_1_out), .in_1(1'b0), .out(multiplexer_4_out));
  Multiplexer multiplexer_5 (.sel(reset), .in_0(multiplexer_2_out), .in_1(1'b0), .out(multiplexer_5_out));
  Multiplexer multiplexer_6 (.sel(reset), .in_0(multiplexer_3_out), .in_1(1'b0), .out(multiplexer_6_out));
  D_FF Q_2_n (.D(multiplexer_4_out), .C(clock), .Q(A));  // open: nQ
  D_FF Q_1_n (.D(multiplexer_5_out), .C(clock), .Q(B));  // open: nQ
  D_FF Q_0_n (.D(multiplexer_6_out), .C(clock), .Q(C));  // open: nQ

  // Other names for the same wires on the sheet: Q_0_n = C; Q_1_n = B; Q_2_n = A

  // Notes on the sheet:
  //   clock: Hz: 2
endmodule

/* Test case T06:
X Y Z reset load clock A B C
0 0 0 1 0 0 x x x
0 0 0 1 0 1 0 0 0
1 1 0 0 1 0 0 0 0
1 1 0 0 1 1 1 1 0
0 0 0 0 0 0 1 1 0
0 0 0 0 0 1 1 1 1
0 0 0 0 0 0 1 1 1
0 0 0 0 0 1 0 0 1
0 0 0 0 0 0 0 0 1
0 0 0 0 0 1 1 0 0
0 0 0 0 0 0 1 0 0
0 0 0 0 0 1 0 1 0
0 0 0 0 0 0 0 1 0
0 0 0 0 0 1 0 1 1
0 0 0 0 0 0 0 1 1
0 0 0 0 0 1 1 0 1
0 0 0 0 0 0 1 0 1
0 0 0 0 0 1 1 1 1
0 0 0 0 0 0 1 1 1
0 0 0 0 0 1 0 0 1
0 0 0 0 0 0 0 0 1
*/
