// Digital circuit finalcedtq3.dig as structural Verilog
module finalcedtq3 (
  input  [7:0] N,
  input  \new ,
  input  reset,
  input  clock,
  output [7:0] num_inc,
  output [7:0] max,
  output busy
);

  wire comparator_1_gt;
  wire [7:0] add_1_s, register_1_q, register_2_q;

  Comparator #(.Bits(8)) comparator_1 (.a(N), .b(max), .gt(comparator_1_gt));  // open: eq, lt
  and and_1 (busy, comparator_1_gt, \new );
  Add #(.Bits(8)) add_1 (.a(num_inc), .b(8'h1), .c_i(1'b0), .s(add_1_s));  // open: c_o
  Register #(.Bits(8)) register_1 (.D(add_1_s), .C(clock), .en(busy), .Q(register_1_q));
  Register #(.Bits(8)) register_2 (.D(N), .C(clock), .en(busy), .Q(register_2_q));
  Multiplexer #(.Bits(8)) multiplexer_1 (.sel(reset), .in_0(register_2_q), .in_1({8{1'b0}}), .out(max));
  Multiplexer #(.Bits(8)) multiplexer_2 (.sel(reset), .in_0(register_1_q), .in_1({8{1'b0}}), .out(num_inc));
endmodule
