// Digital circuit midterm65_1.dig as structural Verilog
module midterm65_1 (
  input  [3:0] In,
  output out
);

  wire and_1_out, and_2_out, and_3_out, and_4_out;

  and and_1 (and_1_out, In[3], In[1], ~In[0]);  // And
  and and_2 (and_2_out, ~In[3], In[2], ~In[1]);  // And
  and and_3 (and_3_out, ~In[3], ~In[2], In[0]);  // And
  and and_4 (and_4_out, ~In[1], In[0]);  // And
  or or_1 (out, and_1_out, and_2_out, and_3_out, and_4_out);
endmodule
