// Digital circuit midterm65_2.dig as structural Verilog
module midterm65_2 (
  input  [2:0] in0,
  input  [2:0] in1,
  input  addsubtract,
  output [2:0] \output 
);

  wire [1:0] add_1_s, add_2_s;
  wire [2:0] add_3_s, and_1_out, and_2_out, sub_1_s;

  Add add_1 (.a(in0[0]), .b(in0[1]), .c_i(in0[2]), .s(add_1_s[0]), .c_o(add_1_s[1]));
  Add add_2 (.a(in1[0]), .b(in1[1]), .c_i(in1[2]), .s(add_2_s[0]), .c_o(add_2_s[1]));
  Add #(.Bits(2)) add_3 (.a(add_1_s), .b(add_2_s), .c_i(1'b0), .s(add_3_s[1:0]), .c_o(add_3_s[2]));
  Sub #(.Bits(2)) sub_1 (.a(add_1_s), .b(add_2_s), .c_i(1'b0), .s(sub_1_s[1:0]), .c_o(sub_1_s[2]));
  assign and_1_out = ~{3{addsubtract}} & add_3_s;  // And and_1, 3 bits wide
  assign and_2_out = {3{addsubtract}} & sub_1_s;  // And and_2, 3 bits wide
  assign \output  = and_1_out | and_2_out;  // Or or_1, 3 bits wide
endmodule
