// Digital circuit premidterm1.dig as structural Verilog
module premidterm1 (
  input  IN1,
  input  IN2,
  input  IN3,
  input  IN4,
  input  IN5,
  input  IN6
);

  wire a, false, nor_1_out, nor_2_out, not_2_out, true;

  Seven_Seg seven_seg_1 (.a(a), .b(true), .c(true), .d(a), .e(a), .f(a), .g(false), .dp(1'b0));
  not not_1 (false, true);
  nor nor_1 (nor_1_out, IN1, IN2, IN4, IN5, IN6);
  nor nor_2 (nor_2_out, IN1, IN2, IN3, IN4, IN5);
  not not_2 (not_2_out, IN1);
  or or_1 (true, not_2_out, IN1);
  or or_2 (a, nor_1_out, nor_2_out);
endmodule
